# Fritzing sketch window-sensor-circuit_RevA (saved by Fritzing 0.9.4)
breadboards: 1

parts:
  BAT1 = Battery Holders [package=lipo-1100mAh]
  S3 = Reed switch [package=THT]
  S4 = Reed switch [package=THT]
  R2 = Resistor [tolerance=±5% resistance=10k package="0805 [SMD]"]
  WeMos_D1_Mini2 = WeMos D1 Mini
  sdsdfs = 74HC595 [package="DIP16 [THT]"]  # not connected

nets:
  N1: BAT1.+, WeMos_D1_Mini2.5V
  N2: BAT1.-, S3.pin_1, R2.Pin_1, WeMos_D1_Mini2.G
  N3: S3.pin_2, WeMos_D1_Mini2.RST
  N4: S4.pin_1, WeMos_D1_Mini2.3V3
  N5: S4.pin_2, WeMos_D1_Mini2.D2
